// Logisim project Logisim Circuits for Project Group 3.circ as structural Verilog: 4 circuits, main circuit Sequential 2
module Basic_Gates (
  input  A,
  input  A_2,
  input  A_3,
  input  A_4,
  input  A_5,
  input  A_6,
  input  in_7,
  input  in_8,
  input  B,
  input  B_2,
  input  B_3,
  input  B_4,
  input  B_5,
  input  B_6,
  input  B_7,
  input  B_8,
  input  C,
  input  C_2,
  input  C_3,
  input  C_4,
  input  C_5,
  input  C_6,
  input  C_7,
  input  C_8,
  output a_7,
  output a_8,
  output a_9,
  output a_10,
  output a_11,
  output a_12,
  output a_13,
  output a_14,
  output b_9,
  output b_10,
  output b_11,
  output b_12,
  output b_13,
  output b_14,
  output b_15,
  output b_16,
  output c_9,
  output c_10,
  output c_11,
  output c_12,
  output c_13,
  output c_14,
  output c_15,
  output c_16,
  output d,
  output d_2,
  output d_3,
  output d_4,
  output d_5,
  output d_6,
  output d_7,
  output d_8,
  output e,
  output e_2,
  output e_3,
  output e_4,
  output e_5,
  output e_6,
  output e_7,
  output e_8,
  output f,
  output f_2,
  output f_3,
  output f_4,
  output f_5,
  output f_6,
  output f_7,
  output f_8,
  output g,
  output g_2,
  output g_3,
  output g_4,
  output g_5,
  output g_6,
  output g_7,
  output g_8
);

  wire and_1_out, and_2_out, and_3_out, and_4_out, and_5_out, and_6_out, and_7_out, and_8_out, and_9_out,
       and_10_out, and_11_out, and_12_out, and_13_out, and_14_out, and_15_out, and_16_out, and_17_out,
       and_18_out, and_19_out, and_20_out, and_21_out, and_22_out, and_23_out, and_24_out, and_25_out,
       and_26_out, and_27_out, and_28_out, and_29_out, and_30_out, and_31_out, and_32_out, and_33_out,
       and_34_out, and_35_out, and_36_out, and_37_out, and_38_out, and_39_out, and_40_out, and_41_out,
       and_42_out, and_43_out, and_44_out, and_45_out, and_46_out, and_47_out, and_48_out, and_49_out,
       and_50_out, and_51_out, and_52_out, and_53_out, and_54_out, and_55_out, and_56_out, and_57_out,
       and_58_out, and_59_out, and_60_out, and_61_out, and_62_out, and_63_out, and_64_out, and_65_out,
       and_66_out, and_67_out, and_68_out, and_69_out, and_70_out, and_71_out, and_72_out, and_73_out,
       and_74_out, and_75_out, and_76_out, and_77_out, and_78_out, and_79_out, and_80_out, and_81_out,
       and_82_out, and_83_out, and_84_out, and_85_out, and_86_out, and_87_out, and_88_out, and_89_out,
       and_90_out, and_91_out, and_92_out, and_93_out, and_94_out, and_95_out, and_96_out, and_97_out,
       and_98_out, and_99_out, and_100_out, and_101_out, and_102_out, and_103_out, and_104_out, and_105_out,
       and_106_out, and_107_out, and_108_out, and_109_out, and_110_out, and_111_out, and_112_out,
       and_113_out, and_114_out, and_115_out, and_116_out, and_117_out, and_118_out, and_119_out,
       and_120_out, not_1_out, not_2_out, not_3_out, not_4_out, not_5_out, not_6_out, not_7_out, not_8_out,
       not_9_out, not_10_out, not_11_out, not_12_out, not_13_out, not_14_out, not_15_out, not_16_out,
       not_17_out, not_18_out, not_19_out, not_20_out, not_21_out, not_22_out, not_23_out, not_24_out,
       not_25_out, not_26_out, not_27_out, not_28_out, not_29_out, not_30_out, not_31_out, not_32_out,
       not_33_out, not_34_out, not_35_out, not_36_out, not_37_out, not_38_out, not_39_out, not_40_out,
       not_41_out, not_42_out, not_43_out, not_44_out, not_45_out, not_46_out, not_47_out, not_48_out,
       not_49_out, not_50_out, not_51_out, not_52_out, not_53_out, not_54_out, not_55_out, not_56_out,
       not_57_out, not_58_out, not_59_out, not_60_out, not_61_out, not_62_out, not_63_out, not_64_out,
       not_65_out, not_66_out, not_67_out, not_68_out, not_69_out, not_70_out, not_71_out, not_72_out,
       not_73_out, not_74_out, not_75_out, not_76_out, not_77_out, not_78_out, not_79_out, not_80_out,
       not_81_out, not_82_out, not_83_out, not_84_out, not_85_out, not_86_out, not_87_out, not_88_out,
       not_89_out, not_90_out, not_91_out, not_92_out, not_93_out, not_94_out, not_95_out, not_96_out,
       not_97_out, not_98_out, not_99_out, not_100_out, not_101_out, not_102_out, not_103_out, not_104_out,
       not_105_out, not_106_out, not_107_out, not_108_out, not_109_out, not_110_out, not_111_out,
       not_112_out, not_113_out, not_114_out, not_115_out, not_116_out, not_117_out, not_118_out,
       not_119_out, not_120_out, not_121_out, not_122_out, not_123_out, not_124_out, not_125_out,
       not_126_out, not_127_out, not_128_out, not_129_out, not_130_out, not_131_out, not_132_out,
       not_133_out, not_134_out, not_135_out, not_136_out, not_137_out, not_138_out, not_139_out,
       not_140_out, not_141_out, not_142_out, not_143_out, not_144_out;

  not not_1 (not_1_out, A);
  not not_2 (not_2_out, B);
  not not_3 (not_3_out, C);
  not not_4 (not_4_out, B);
  not not_5 (not_5_out, B);
  and and_1 (and_1_out, A, C);
  not not_6 (not_6_out, A);
  not not_7 (not_7_out, C);
  not not_8 (not_8_out, C);
  not not_9 (not_9_out, B);
  not not_10 (not_10_out, B);
  not not_11 (not_11_out, C);
  not not_12 (not_12_out, A);
  not not_13 (not_13_out, C);
  not not_14 (not_14_out, B);
  not not_15 (not_15_out, A);
  not not_16 (not_16_out, B);
  not not_17 (not_17_out, A);
  not not_18 (not_18_out, C);
  and and_2 (and_2_out, not_1_out, not_2_out);
  and and_3 (and_3_out, B, not_3_out);
  and and_4 (and_4_out, A, C);
  and and_5 (and_5_out, not_4_out, C);
  or or_1 (c_9, not_5_out, and_1_out);
  and and_6 (and_6_out, not_6_out, not_7_out);
  and and_7 (and_7_out, B, not_8_out);
  and and_8 (and_8_out, A, not_9_out, C);
  and and_9 (and_9_out, not_10_out, C);
  and and_10 (and_10_out, B, not_11_out);
  and and_11 (and_11_out, not_12_out, not_13_out);
  and and_12 (and_12_out, not_14_out, C);
  and and_13 (and_13_out, not_15_out, not_16_out);
  and and_14 (and_14_out, not_17_out, C);
  and and_15 (and_15_out, A, B, not_18_out);
  or or_2 (a_7, and_2_out, and_3_out, and_4_out);
  or or_3 (b_9, and_5_out, A);
  or or_4 (d, and_6_out, and_7_out, and_8_out);
  or or_5 (e, and_9_out, and_10_out);
  or or_6 (f, and_11_out, and_12_out);
  or or_7 (g, and_13_out, and_14_out, and_15_out);
  _7_Segment_Display u_7_segment_display_1 (.g(g), .f(f), .a(a_7), .b(b_9), .e(e), .d(d), .c(c_9));  // open: dp
  not not_19 (not_19_out, A_2);
  not not_20 (not_20_out, B_2);
  not not_21 (not_21_out, C_2);
  not not_22 (not_22_out, B_2);
  not not_23 (not_23_out, B_2);
  and and_16 (and_16_out, A_2, C_2);
  not not_24 (not_24_out, A_2);
  not not_25 (not_25_out, C_2);
  not not_26 (not_26_out, C_2);
  not not_27 (not_27_out, B_2);
  not not_28 (not_28_out, B_2);
  not not_29 (not_29_out, C_2);
  not not_30 (not_30_out, A_2);
  not not_31 (not_31_out, C_2);
  not not_32 (not_32_out, B_2);
  not not_33 (not_33_out, A_2);
  not not_34 (not_34_out, B_2);
  not not_35 (not_35_out, A_2);
  not not_36 (not_36_out, C_2);
  and and_17 (and_17_out, not_19_out, not_20_out);
  and and_18 (and_18_out, B_2, not_21_out);
  and and_19 (and_19_out, A_2, C_2);
  and and_20 (and_20_out, not_22_out, C_2);
  or or_8 (c_10, not_23_out, and_16_out);
  and and_21 (and_21_out, not_24_out, not_25_out);
  and and_22 (and_22_out, B_2, not_26_out);
  and and_23 (and_23_out, A_2, not_27_out, C_2);
  and and_24 (and_24_out, not_28_out, C_2);
  and and_25 (and_25_out, B_2, not_29_out);
  and and_26 (and_26_out, not_30_out, not_31_out);
  and and_27 (and_27_out, not_32_out, C_2);
  and and_28 (and_28_out, not_33_out, not_34_out);
  and and_29 (and_29_out, not_35_out, C_2);
  and and_30 (and_30_out, A_2, B_2, not_36_out);
  or or_9 (a_8, and_17_out, and_18_out, and_19_out);
  or or_10 (b_10, and_20_out, A_2);
  or or_11 (d_2, and_21_out, and_22_out, and_23_out);
  or or_12 (e_2, and_24_out, and_25_out);
  or or_13 (f_2, and_26_out, and_27_out);
  or or_14 (g_2, and_28_out, and_29_out, and_30_out);
  _7_Segment_Display u_7_segment_display_2 (
    .g(g_2), .f(f_2), .a(a_8), .b(b_10), .e(e_2), .d(d_2), .c(c_10));  // open: dp
  not not_37 (not_37_out, A_3);
  not not_38 (not_38_out, B_3);
  not not_39 (not_39_out, C_3);
  not not_40 (not_40_out, B_3);
  not not_41 (not_41_out, B_3);
  and and_31 (and_31_out, A_3, C_3);
  not not_42 (not_42_out, A_3);
  not not_43 (not_43_out, C_3);
  not not_44 (not_44_out, C_3);
  not not_45 (not_45_out, B_3);
  not not_46 (not_46_out, B_3);
  not not_47 (not_47_out, C_3);
  not not_48 (not_48_out, A_3);
  not not_49 (not_49_out, C_3);
  not not_50 (not_50_out, B_3);
  not not_51 (not_51_out, A_3);
  not not_52 (not_52_out, B_3);
  not not_53 (not_53_out, A_3);
  not not_54 (not_54_out, C_3);
  and and_32 (and_32_out, not_37_out, not_38_out);
  and and_33 (and_33_out, B_3, not_39_out);
  or or_15 (a_9, and_32_out, and_33_out, and_34_out);
  and and_34 (and_34_out, A_3, C_3);
  and and_35 (and_35_out, not_40_out, C_3);
  or or_16 (b_11, and_35_out, A_3);
  or or_17 (c_11, not_41_out, and_31_out);
  and and_36 (and_36_out, not_42_out, not_43_out);
  or or_18 (d_3, and_36_out, and_37_out, and_38_out);
  and and_37 (and_37_out, B_3, not_44_out);
  and and_38 (and_38_out, A_3, not_45_out, C_3);
  and and_39 (and_39_out, not_46_out, C_3);
  or or_19 (e_3, and_39_out, and_40_out);
  and and_40 (and_40_out, B_3, not_47_out);
  and and_41 (and_41_out, not_48_out, not_49_out);
  or or_20 (f_3, and_41_out, and_42_out);
  and and_42 (and_42_out, not_50_out, C_3);
  and and_43 (and_43_out, not_51_out, not_52_out);
  and and_44 (and_44_out, not_53_out, C_3);
  or or_21 (g_3, and_43_out, and_44_out, and_45_out);
  and and_45 (and_45_out, A_3, B_3, not_54_out);
  _7_Segment_Display u_7_segment_display_3 (
    .g(g_3), .f(f_3), .a(a_9), .b(b_11), .e(e_3), .d(d_3), .c(c_11));  // open: dp
  not not_55 (not_55_out, A_4);
  not not_56 (not_56_out, B_4);
  not not_57 (not_57_out, C_4);
  not not_58 (not_58_out, B_4);
  not not_59 (not_59_out, B_4);
  and and_46 (and_46_out, A_4, C_4);
  not not_60 (not_60_out, A_4);
  not not_61 (not_61_out, C_4);
  not not_62 (not_62_out, C_4);
  not not_63 (not_63_out, B_4);
  not not_64 (not_64_out, B_4);
  not not_65 (not_65_out, C_4);
  not not_66 (not_66_out, A_4);
  not not_67 (not_67_out, C_4);
  not not_68 (not_68_out, B_4);
  not not_69 (not_69_out, A_4);
  not not_70 (not_70_out, B_4);
  not not_71 (not_71_out, A_4);
  not not_72 (not_72_out, C_4);
  and and_47 (and_47_out, not_55_out, not_56_out);
  and and_48 (and_48_out, B_4, not_57_out);
  or or_22 (a_10, and_47_out, and_48_out, and_49_out);
  and and_49 (and_49_out, A_4, C_4);
  and and_50 (and_50_out, not_58_out, C_4);
  or or_23 (b_12, and_50_out, A_4);
  or or_24 (c_12, not_59_out, and_46_out);
  and and_51 (and_51_out, not_60_out, not_61_out);
  and and_52 (and_52_out, B_4, not_62_out);
  or or_25 (d_4, and_51_out, and_52_out, and_53_out);
  and and_53 (and_53_out, A_4, not_63_out, C_4);
  and and_54 (and_54_out, not_64_out, C_4);
  or or_26 (e_4, and_54_out, and_55_out);
  and and_55 (and_55_out, B_4, not_65_out);
  and and_56 (and_56_out, not_66_out, not_67_out);
  or or_27 (f_4, and_56_out, and_57_out);
  and and_57 (and_57_out, not_68_out, C_4);
  and and_58 (and_58_out, not_69_out, not_70_out);
  and and_59 (and_59_out, not_71_out, C_4);
  or or_28 (g_4, and_58_out, and_59_out, and_60_out);
  and and_60 (and_60_out, A_4, B_4, not_72_out);
  _7_Segment_Display u_7_segment_display_4 (
    .g(g_4), .f(f_4), .a(a_10), .b(b_12), .e(e_4), .d(d_4), .c(c_12));  // open: dp
  not not_73 (not_73_out, A_5);
  not not_74 (not_74_out, B_5);
  not not_75 (not_75_out, C_5);
  not not_76 (not_76_out, B_5);
  not not_77 (not_77_out, B_5);
  and and_61 (and_61_out, A_5, C_5);
  not not_78 (not_78_out, A_5);
  not not_79 (not_79_out, C_5);
  not not_80 (not_80_out, C_5);
  not not_81 (not_81_out, B_5);
  not not_82 (not_82_out, B_5);
  not not_83 (not_83_out, C_5);
  not not_84 (not_84_out, A_5);
  not not_85 (not_85_out, C_5);
  not not_86 (not_86_out, B_5);
  not not_87 (not_87_out, A_5);
  not not_88 (not_88_out, B_5);
  not not_89 (not_89_out, A_5);
  not not_90 (not_90_out, C_5);
  and and_62 (and_62_out, not_73_out, not_74_out);
  and and_63 (and_63_out, B_5, not_75_out);
  and and_64 (and_64_out, A_5, C_5);
  and and_65 (and_65_out, not_76_out, C_5);
  or or_29 (c_13, not_77_out, and_61_out);
  and and_66 (and_66_out, not_78_out, not_79_out);
  and and_67 (and_67_out, B_5, not_80_out);
  and and_68 (and_68_out, A_5, not_81_out, C_5);
  and and_69 (and_69_out, not_82_out, C_5);
  and and_70 (and_70_out, B_5, not_83_out);
  and and_71 (and_71_out, not_84_out, not_85_out);
  and and_72 (and_72_out, not_86_out, C_5);
  and and_73 (and_73_out, not_87_out, not_88_out);
  and and_74 (and_74_out, not_89_out, C_5);
  and and_75 (and_75_out, A_5, B_5, not_90_out);
  or or_30 (a_11, and_62_out, and_63_out, and_64_out);
  or or_31 (b_13, and_65_out, A_5);
  or or_32 (d_5, and_66_out, and_67_out, and_68_out);
  or or_33 (e_5, and_69_out, and_70_out);
  or or_34 (f_5, and_71_out, and_72_out);
  or or_35 (g_5, and_73_out, and_74_out, and_75_out);
  _7_Segment_Display u_7_segment_display_5 (
    .g(g_5), .f(f_5), .a(a_11), .b(b_13), .e(e_5), .d(d_5), .c(c_13));  // open: dp
  not not_91 (not_91_out, A_6);
  not not_92 (not_92_out, B_6);
  not not_93 (not_93_out, C_6);
  not not_94 (not_94_out, B_6);
  not not_95 (not_95_out, B_6);
  and and_76 (and_76_out, A_6, C_6);
  not not_96 (not_96_out, A_6);
  not not_97 (not_97_out, C_6);
  not not_98 (not_98_out, C_6);
  not not_99 (not_99_out, B_6);
  not not_100 (not_100_out, B_6);
  not not_101 (not_101_out, C_6);
  not not_102 (not_102_out, A_6);
  not not_103 (not_103_out, C_6);
  not not_104 (not_104_out, B_6);
  not not_105 (not_105_out, A_6);
  not not_106 (not_106_out, B_6);
  not not_107 (not_107_out, A_6);
  not not_108 (not_108_out, C_6);
  and and_77 (and_77_out, not_91_out, not_92_out);
  and and_78 (and_78_out, B_6, not_93_out);
  and and_79 (and_79_out, A_6, C_6);
  and and_80 (and_80_out, not_94_out, C_6);
  or or_36 (c_14, not_95_out, and_76_out);
  and and_81 (and_81_out, not_96_out, not_97_out);
  and and_82 (and_82_out, B_6, not_98_out);
  and and_83 (and_83_out, A_6, not_99_out, C_6);
  and and_84 (and_84_out, not_100_out, C_6);
  and and_85 (and_85_out, B_6, not_101_out);
  and and_86 (and_86_out, not_102_out, not_103_out);
  and and_87 (and_87_out, not_104_out, C_6);
  and and_88 (and_88_out, not_105_out, not_106_out);
  and and_89 (and_89_out, not_107_out, C_6);
  and and_90 (and_90_out, A_6, B_6, not_108_out);
  or or_37 (a_12, and_77_out, and_78_out, and_79_out);
  or or_38 (b_14, and_80_out, A_6);
  or or_39 (d_6, and_81_out, and_82_out, and_83_out);
  or or_40 (e_6, and_84_out, and_85_out);
  or or_41 (f_6, and_86_out, and_87_out);
  or or_42 (g_6, and_88_out, and_89_out, and_90_out);
  _7_Segment_Display u_7_segment_display_6 (
    .g(g_6), .f(f_6), .a(a_12), .b(b_14), .e(e_6), .d(d_6), .c(c_14));  // open: dp
  not not_109 (not_109_out, in_7);
  not not_110 (not_110_out, B_7);
  not not_111 (not_111_out, C_7);
  not not_112 (not_112_out, B_7);
  not not_113 (not_113_out, B_7);
  and and_91 (and_91_out, in_7, C_7);
  not not_114 (not_114_out, in_7);
  not not_115 (not_115_out, C_7);
  not not_116 (not_116_out, C_7);
  not not_117 (not_117_out, B_7);
  not not_118 (not_118_out, B_7);
  not not_119 (not_119_out, C_7);
  not not_120 (not_120_out, in_7);
  not not_121 (not_121_out, C_7);
  not not_122 (not_122_out, B_7);
  not not_123 (not_123_out, in_7);
  not not_124 (not_124_out, B_7);
  not not_125 (not_125_out, in_7);
  not not_126 (not_126_out, C_7);
  and and_92 (and_92_out, not_109_out, not_110_out);
  and and_93 (and_93_out, B_7, not_111_out);
  and and_94 (and_94_out, in_7, C_7);
  and and_95 (and_95_out, not_112_out, C_7);
  or or_43 (c_15, not_113_out, and_91_out);
  and and_96 (and_96_out, not_114_out, not_115_out);
  and and_97 (and_97_out, B_7, not_116_out);
  and and_98 (and_98_out, in_7, not_117_out, C_7);
  and and_99 (and_99_out, not_118_out, C_7);
  and and_100 (and_100_out, B_7, not_119_out);
  and and_101 (and_101_out, not_120_out, not_121_out);
  and and_102 (and_102_out, not_122_out, C_7);
  and and_103 (and_103_out, not_123_out, not_124_out);
  and and_104 (and_104_out, not_125_out, C_7);
  and and_105 (and_105_out, in_7, B_7, not_126_out);
  or or_44 (a_13, and_92_out, and_93_out, and_94_out);
  or or_45 (b_15, and_95_out, in_7);
  or or_46 (d_7, and_96_out, and_97_out, and_98_out);
  or or_47 (e_7, and_99_out, and_100_out);
  or or_48 (f_7, and_101_out, and_102_out);
  or or_49 (g_7, and_103_out, and_104_out, and_105_out);
  _7_Segment_Display u_7_segment_display_7 (
    .g(g_7), .f(f_7), .a(a_13), .b(b_15), .e(e_7), .d(d_7), .c(c_15));  // open: dp
  not not_127 (not_127_out, in_8);
  not not_128 (not_128_out, B_8);
  not not_129 (not_129_out, C_8);
  not not_130 (not_130_out, B_8);
  not not_131 (not_131_out, B_8);
  and and_106 (and_106_out, in_8, C_8);
  not not_132 (not_132_out, in_8);
  not not_133 (not_133_out, C_8);
  not not_134 (not_134_out, C_8);
  not not_135 (not_135_out, B_8);
  not not_136 (not_136_out, B_8);
  not not_137 (not_137_out, C_8);
  not not_138 (not_138_out, in_8);
  not not_139 (not_139_out, C_8);
  not not_140 (not_140_out, B_8);
  not not_141 (not_141_out, in_8);
  not not_142 (not_142_out, B_8);
  not not_143 (not_143_out, in_8);
  not not_144 (not_144_out, C_8);
  and and_107 (and_107_out, not_127_out, not_128_out);
  and and_108 (and_108_out, B_8, not_129_out);
  and and_109 (and_109_out, in_8, C_8);
  and and_110 (and_110_out, not_130_out, C_8);
  or or_50 (c_16, not_131_out, and_106_out);
  and and_111 (and_111_out, not_132_out, not_133_out);
  and and_112 (and_112_out, B_8, not_134_out);
  and and_113 (and_113_out, in_8, not_135_out, C_8);
  and and_114 (and_114_out, not_136_out, C_8);
  and and_115 (and_115_out, B_8, not_137_out);
  and and_116 (and_116_out, not_138_out, not_139_out);
  and and_117 (and_117_out, not_140_out, C_8);
  and and_118 (and_118_out, not_141_out, not_142_out);
  and and_119 (and_119_out, not_143_out, C_8);
  and and_120 (and_120_out, in_8, B_8, not_144_out);
  or or_51 (a_14, and_107_out, and_108_out, and_109_out);
  or or_52 (b_16, and_110_out, in_8);
  or or_53 (d_8, and_111_out, and_112_out, and_113_out);
  or or_54 (e_8, and_114_out, and_115_out);
  or or_55 (f_8, and_116_out, and_117_out);
  or or_56 (g_8, and_118_out, and_119_out, and_120_out);
  _7_Segment_Display u_7_segment_display_8 (
    .g(g_8), .f(f_8), .a(a_14), .b(b_16), .e(e_8), .d(d_8), .c(c_16));  // open: dp

  // Notes on the sheet:
  //   Group 3
  //   Group 3
endmodule

module Nand_Gates (
  input  A,
  input  A_2,
  input  A_3,
  input  A_4,
  input  B,
  input  B_2,
  input  B_3,
  input  B_4,
  input  C,
  input  C_2,
  input  C_3,
  input  C_4,
  input  A_5,
  input  A_6,
  input  A_7,
  input  A_8,
  input  B_5,
  input  B_6,
  input  B_7,
  input  B_8,
  input  C_5,
  input  C_6,
  input  C_7,
  input  C_8,
  output a_9,
  output a_10,
  output a_11,
  output a_12,
  output b_9,
  output b_10,
  output b_11,
  output b_12,
  output c_9,
  output c_10,
  output c_11,
  output c_12,
  output d,
  output d_2,
  output d_3,
  output d_4,
  output e,
  output e_2,
  output e_3,
  output e_4,
  output f,
  output f_2,
  output f_3,
  output f_4,
  output g,
  output g_2,
  output g_3,
  output g_4,
  output a_13,
  output a_14,
  output a_15,
  output a_16,
  output b_13,
  output b_14,
  output b_15,
  output b_16,
  output c_13,
  output c_14,
  output c_15,
  output c_16,
  output d_5,
  output d_6,
  output d_7,
  output d_8,
  output e_5,
  output e_6,
  output e_7,
  output e_8,
  output f_5,
  output f_6,
  output f_7,
  output f_8,
  output g_5,
  output g_6,
  output g_7,
  output g_8
);

  wire nand_1_out, nand_2_out, nand_3_out, nand_4_out, nand_5_out, nand_6_out, nand_7_out, nand_8_out,
       nand_9_out, nand_10_out, nand_11_out, nand_12_out, nand_13_out, nand_14_out, nand_15_out, nand_16_out,
       nand_17_out, nand_18_out, nand_19_out, nand_20_out, nand_21_out, nand_22_out, nand_23_out,
       nand_24_out, nand_25_out, nand_26_out, nand_27_out, nand_28_out, nand_29_out, nand_30_out,
       nand_31_out, nand_32_out, nand_33_out, nand_34_out, nand_35_out, nand_36_out, nand_37_out,
       nand_38_out, nand_39_out, nand_40_out, nand_41_out, nand_43_out, nand_44_out, nand_45_out,
       nand_46_out, nand_47_out, nand_48_out, nand_49_out, nand_50_out, nand_51_out, nand_52_out,
       nand_53_out, nand_54_out, nand_55_out, nand_56_out, nand_57_out, nand_59_out, nand_60_out,
       nand_61_out, nand_62_out, nand_63_out, nand_64_out, nand_65_out, nand_66_out, nand_67_out,
       nand_68_out, nand_81_out, nand_82_out, nand_83_out, nand_84_out, nand_85_out, nand_86_out,
       nand_87_out, nand_88_out, nand_89_out, nand_90_out, nand_91_out, nand_92_out, nand_93_out,
       nand_94_out, nand_95_out, nand_96_out, nand_97_out, nand_98_out, nand_99_out, nand_100_out,
       nand_101_out, nand_102_out, nand_103_out, nand_104_out, nand_105_out, nand_106_out, nand_107_out,
       nand_108_out, nand_109_out, nand_110_out, nand_111_out, nand_112_out, nand_113_out, nand_114_out,
       nand_115_out, nand_116_out, nand_117_out, nand_118_out, nand_119_out, nand_120_out, nand_121_out,
       nand_123_out, nand_124_out, nand_125_out, nand_126_out, nand_127_out, nand_128_out, nand_129_out,
       nand_130_out, nand_131_out, nand_132_out, nand_133_out, nand_134_out, nand_135_out, nand_136_out,
       nand_137_out, nand_139_out, nand_140_out, nand_141_out, nand_142_out, nand_143_out, nand_144_out,
       nand_145_out, nand_146_out, nand_147_out, nand_148_out, nand_161_out, nand_162_out, nand_163_out,
       nand_164_out, nand_165_out, nand_166_out, nand_167_out, nand_168_out, nand_169_out, nand_170_out,
       nand_171_out, nand_172_out, nand_173_out, nand_174_out, nand_175_out, nand_176_out, nand_177_out,
       nand_178_out, nand_179_out, nand_180_out, nand_181_out, nand_182_out, nand_183_out, nand_184_out,
       nand_185_out, nand_186_out, nand_187_out, nand_188_out, nand_189_out, nand_190_out, nand_191_out,
       nand_192_out, nand_193_out, nand_194_out, nand_195_out, nand_196_out, nand_197_out, nand_198_out,
       nand_199_out, nand_200_out, nand_201_out, nand_203_out, nand_204_out, nand_205_out, nand_206_out,
       nand_207_out, nand_208_out, nand_209_out, nand_210_out, nand_211_out, nand_212_out, nand_213_out,
       nand_214_out, nand_215_out, nand_216_out, nand_217_out, nand_219_out, nand_220_out, nand_221_out,
       nand_222_out, nand_223_out, nand_224_out, nand_225_out, nand_226_out, nand_227_out, nand_228_out,
       nand_241_out, nand_242_out, nand_243_out, nand_244_out, nand_245_out, nand_246_out, nand_247_out,
       nand_248_out, nand_249_out, nand_250_out, nand_251_out, nand_252_out, nand_253_out, nand_254_out,
       nand_255_out, nand_256_out, nand_257_out, nand_258_out, nand_259_out, nand_260_out, nand_261_out,
       nand_262_out, nand_263_out, nand_264_out, nand_265_out, nand_266_out, nand_267_out, nand_268_out,
       nand_269_out, nand_270_out, nand_271_out, nand_272_out, nand_273_out, nand_274_out, nand_275_out,
       nand_276_out, nand_277_out, nand_278_out, nand_279_out, nand_280_out, nand_281_out, nand_283_out,
       nand_284_out, nand_285_out, nand_286_out, nand_287_out, nand_288_out, nand_289_out, nand_290_out,
       nand_291_out, nand_292_out, nand_293_out, nand_294_out, nand_295_out, nand_296_out, nand_297_out,
       nand_299_out, nand_300_out, nand_301_out, nand_302_out, nand_303_out, nand_304_out, nand_305_out,
       nand_306_out, nand_307_out, nand_308_out;

  nand nand_1 (nand_1_out, A, A);
  nand nand_2 (nand_2_out, B, B);
  nand nand_3 (nand_3_out, C, C);
  nand nand_4 (nand_4_out, B, B);
  nand nand_5 (nand_5_out, A, C);
  nand nand_6 (nand_6_out, A, A);
  nand nand_7 (nand_7_out, C, C);
  nand nand_8 (nand_8_out, C, C);
  nand nand_9 (nand_9_out, B, B);
  nand nand_10 (nand_10_out, B, B);
  nand nand_11 (nand_11_out, C, C);
  nand nand_12 (nand_12_out, A, A);
  nand nand_13 (nand_13_out, C, C);
  nand nand_14 (nand_14_out, B, B);
  nand nand_15 (nand_15_out, A, A);
  nand nand_16 (nand_16_out, B, B);
  nand nand_17 (nand_17_out, A, A);
  nand nand_18 (nand_18_out, C, C);
  nand nand_19 (nand_19_out, A_5, A_5);
  nand nand_20 (nand_20_out, B_5, B_5);
  nand nand_21 (nand_21_out, C_5, C_5);
  nand nand_22 (nand_22_out, B_5, B_5);
  nand nand_23 (nand_23_out, A_5, C_5);
  nand nand_24 (nand_24_out, A_5, A_5);
  nand nand_25 (nand_25_out, C_5, C_5);
  nand nand_26 (nand_26_out, C_5, C_5);
  nand nand_27 (nand_27_out, B_5, B_5);
  nand nand_28 (nand_28_out, B_5, B_5);
  nand nand_29 (nand_29_out, C_5, C_5);
  nand nand_30 (nand_30_out, A_5, A_5);
  nand nand_31 (nand_31_out, C_5, C_5);
  nand nand_32 (nand_32_out, B_5, B_5);
  nand nand_33 (nand_33_out, A_5, A_5);
  nand nand_34 (nand_34_out, B_5, B_5);
  nand nand_35 (nand_35_out, A_5, A_5);
  nand nand_36 (nand_36_out, C_5, C_5);
  nand nand_37 (nand_37_out, nand_1_out, nand_2_out);
  nand nand_38 (nand_38_out, B, nand_3_out);
  nand nand_39 (nand_39_out, A, C);
  nand nand_40 (nand_40_out, nand_4_out, C);
  nand nand_41 (nand_41_out, A, A);
  nand nand_42 (c_9, B, nand_5_out);
  nand nand_43 (nand_43_out, nand_6_out, nand_7_out);
  nand nand_44 (nand_44_out, B, nand_8_out);
  nand nand_45 (nand_45_out, A, nand_9_out, C);
  nand nand_46 (nand_46_out, nand_10_out, C);
  nand nand_47 (nand_47_out, B, nand_11_out);
  nand nand_48 (nand_48_out, nand_12_out, nand_13_out);
  nand nand_49 (nand_49_out, nand_14_out, C);
  nand nand_50 (nand_50_out, nand_15_out, nand_16_out);
  nand nand_51 (nand_51_out, nand_17_out, C);
  nand nand_52 (nand_52_out, A, B, nand_18_out);
  nand nand_53 (nand_53_out, nand_19_out, nand_20_out);
  nand nand_54 (nand_54_out, B_5, nand_21_out);
  nand nand_55 (nand_55_out, A_5, C_5);
  nand nand_56 (nand_56_out, nand_22_out, C_5);
  nand nand_57 (nand_57_out, A_5, A_5);
  nand nand_58 (c_13, B_5, nand_23_out);
  nand nand_59 (nand_59_out, nand_24_out, nand_25_out);
  nand nand_60 (nand_60_out, B_5, nand_26_out);
  nand nand_61 (nand_61_out, A_5, nand_27_out, C_5);
  nand nand_62 (nand_62_out, nand_28_out, C_5);
  nand nand_63 (nand_63_out, B_5, nand_29_out);
  nand nand_64 (nand_64_out, nand_30_out, nand_31_out);
  nand nand_65 (nand_65_out, nand_32_out, C_5);
  nand nand_66 (nand_66_out, nand_33_out, nand_34_out);
  nand nand_67 (nand_67_out, nand_35_out, C_5);
  nand nand_68 (nand_68_out, A_5, B_5, nand_36_out);
  nand nand_69 (a_9, nand_37_out, nand_38_out, nand_39_out);
  nand nand_70 (b_9, nand_40_out, nand_41_out);
  nand nand_71 (d, nand_43_out, nand_44_out, nand_45_out);
  nand nand_72 (e, nand_46_out, nand_47_out);
  nand nand_73 (f, nand_48_out, nand_49_out);
  nand nand_74 (g, nand_50_out, nand_51_out, nand_52_out);
  nand nand_75 (a_13, nand_53_out, nand_54_out, nand_55_out);
  nand nand_76 (b_13, nand_56_out, nand_57_out);
  nand nand_77 (d_5, nand_59_out, nand_60_out, nand_61_out);
  nand nand_78 (e_5, nand_62_out, nand_63_out);
  nand nand_79 (f_5, nand_64_out, nand_65_out);
  nand nand_80 (g_5, nand_66_out, nand_67_out, nand_68_out);
  _7_Segment_Display u_7_segment_display_1 (.g(g), .f(f), .a(a_9), .b(b_9), .e(e), .d(d), .c(c_9));  // open: dp
  _7_Segment_Display u_7_segment_display_2 (
    .g(g_5), .f(f_5), .a(a_13), .b(b_13), .e(e_5), .d(d_5), .c(c_13));  // open: dp
  nand nand_81 (nand_81_out, A_2, A_2);
  nand nand_82 (nand_82_out, B_2, B_2);
  nand nand_83 (nand_83_out, C_2, C_2);
  nand nand_84 (nand_84_out, B_2, B_2);
  nand nand_85 (nand_85_out, A_2, C_2);
  nand nand_86 (nand_86_out, A_2, A_2);
  nand nand_87 (nand_87_out, C_2, C_2);
  nand nand_88 (nand_88_out, C_2, C_2);
  nand nand_89 (nand_89_out, B_2, B_2);
  nand nand_90 (nand_90_out, B_2, B_2);
  nand nand_91 (nand_91_out, C_2, C_2);
  nand nand_92 (nand_92_out, A_2, A_2);
  nand nand_93 (nand_93_out, C_2, C_2);
  nand nand_94 (nand_94_out, B_2, B_2);
  nand nand_95 (nand_95_out, A_2, A_2);
  nand nand_96 (nand_96_out, B_2, B_2);
  nand nand_97 (nand_97_out, A_2, A_2);
  nand nand_98 (nand_98_out, C_2, C_2);
  nand nand_99 (nand_99_out, A_6, A_6);
  nand nand_100 (nand_100_out, B_6, B_6);
  nand nand_101 (nand_101_out, C_6, C_6);
  nand nand_102 (nand_102_out, B_6, B_6);
  nand nand_103 (nand_103_out, A_6, C_6);
  nand nand_104 (nand_104_out, A_6, A_6);
  nand nand_105 (nand_105_out, C_6, C_6);
  nand nand_106 (nand_106_out, C_6, C_6);
  nand nand_107 (nand_107_out, B_6, B_6);
  nand nand_108 (nand_108_out, B_6, B_6);
  nand nand_109 (nand_109_out, C_6, C_6);
  nand nand_110 (nand_110_out, A_6, A_6);
  nand nand_111 (nand_111_out, C_6, C_6);
  nand nand_112 (nand_112_out, B_6, B_6);
  nand nand_113 (nand_113_out, A_6, A_6);
  nand nand_114 (nand_114_out, B_6, B_6);
  nand nand_115 (nand_115_out, A_6, A_6);
  nand nand_116 (nand_116_out, C_6, C_6);
  nand nand_117 (nand_117_out, nand_81_out, nand_82_out);
  nand nand_118 (nand_118_out, B_2, nand_83_out);
  nand nand_119 (nand_119_out, A_2, C_2);
  nand nand_120 (nand_120_out, nand_84_out, C_2);
  nand nand_121 (nand_121_out, A_2, A_2);
  nand nand_122 (c_10, B_2, nand_85_out);
  nand nand_123 (nand_123_out, nand_86_out, nand_87_out);
  nand nand_124 (nand_124_out, B_2, nand_88_out);
  nand nand_125 (nand_125_out, A_2, nand_89_out, C_2);
  nand nand_126 (nand_126_out, nand_90_out, C_2);
  nand nand_127 (nand_127_out, B_2, nand_91_out);
  nand nand_128 (nand_128_out, nand_92_out, nand_93_out);
  nand nand_129 (nand_129_out, nand_94_out, C_2);
  nand nand_130 (nand_130_out, nand_95_out, nand_96_out);
  nand nand_131 (nand_131_out, nand_97_out, C_2);
  nand nand_132 (nand_132_out, A_2, B_2, nand_98_out);
  nand nand_133 (nand_133_out, nand_99_out, nand_100_out);
  nand nand_134 (nand_134_out, B_6, nand_101_out);
  nand nand_135 (nand_135_out, A_6, C_6);
  nand nand_136 (nand_136_out, nand_102_out, C_6);
  nand nand_137 (nand_137_out, A_6, A_6);
  nand nand_138 (c_14, B_6, nand_103_out);
  nand nand_139 (nand_139_out, nand_104_out, nand_105_out);
  nand nand_140 (nand_140_out, B_6, nand_106_out);
  nand nand_141 (nand_141_out, A_6, nand_107_out, C_6);
  nand nand_142 (nand_142_out, nand_108_out, C_6);
  nand nand_143 (nand_143_out, B_6, nand_109_out);
  nand nand_144 (nand_144_out, nand_110_out, nand_111_out);
  nand nand_145 (nand_145_out, nand_112_out, C_6);
  nand nand_146 (nand_146_out, nand_113_out, nand_114_out);
  nand nand_147 (nand_147_out, nand_115_out, C_6);
  nand nand_148 (nand_148_out, A_6, B_6, nand_116_out);
  nand nand_149 (a_10, nand_117_out, nand_118_out, nand_119_out);
  nand nand_150 (b_10, nand_120_out, nand_121_out);
  nand nand_151 (d_2, nand_123_out, nand_124_out, nand_125_out);
  nand nand_152 (e_2, nand_126_out, nand_127_out);
  nand nand_153 (f_2, nand_128_out, nand_129_out);
  nand nand_154 (g_2, nand_130_out, nand_131_out, nand_132_out);
  nand nand_155 (a_14, nand_133_out, nand_134_out, nand_135_out);
  nand nand_156 (b_14, nand_136_out, nand_137_out);
  nand nand_157 (d_6, nand_139_out, nand_140_out, nand_141_out);
  nand nand_158 (e_6, nand_142_out, nand_143_out);
  nand nand_159 (f_6, nand_144_out, nand_145_out);
  nand nand_160 (g_6, nand_146_out, nand_147_out, nand_148_out);
  _7_Segment_Display u_7_segment_display_3 (
    .g(g_2), .f(f_2), .a(a_10), .b(b_10), .e(e_2), .d(d_2), .c(c_10));  // open: dp
  _7_Segment_Display u_7_segment_display_4 (
    .g(g_6), .f(f_6), .a(a_14), .b(b_14), .e(e_6), .d(d_6), .c(c_14));  // open: dp
  nand nand_161 (nand_161_out, A_3, A_3);
  nand nand_162 (nand_162_out, B_3, B_3);
  nand nand_163 (nand_163_out, C_3, C_3);
  nand nand_164 (nand_164_out, B_3, B_3);
  nand nand_165 (nand_165_out, A_3, C_3);
  nand nand_166 (nand_166_out, A_3, A_3);
  nand nand_167 (nand_167_out, C_3, C_3);
  nand nand_168 (nand_168_out, C_3, C_3);
  nand nand_169 (nand_169_out, B_3, B_3);
  nand nand_170 (nand_170_out, B_3, B_3);
  nand nand_171 (nand_171_out, C_3, C_3);
  nand nand_172 (nand_172_out, A_3, A_3);
  nand nand_173 (nand_173_out, C_3, C_3);
  nand nand_174 (nand_174_out, B_3, B_3);
  nand nand_175 (nand_175_out, A_3, A_3);
  nand nand_176 (nand_176_out, B_3, B_3);
  nand nand_177 (nand_177_out, A_3, A_3);
  nand nand_178 (nand_178_out, C_3, C_3);
  nand nand_179 (nand_179_out, A_7, A_7);
  nand nand_180 (nand_180_out, B_7, B_7);
  nand nand_181 (nand_181_out, C_7, C_7);
  nand nand_182 (nand_182_out, B_7, B_7);
  nand nand_183 (nand_183_out, A_7, C_7);
  nand nand_184 (nand_184_out, A_7, A_7);
  nand nand_185 (nand_185_out, C_7, C_7);
  nand nand_186 (nand_186_out, C_7, C_7);
  nand nand_187 (nand_187_out, B_7, B_7);
  nand nand_188 (nand_188_out, B_7, B_7);
  nand nand_189 (nand_189_out, C_7, C_7);
  nand nand_190 (nand_190_out, A_7, A_7);
  nand nand_191 (nand_191_out, C_7, C_7);
  nand nand_192 (nand_192_out, B_7, B_7);
  nand nand_193 (nand_193_out, A_7, A_7);
  nand nand_194 (nand_194_out, B_7, B_7);
  nand nand_195 (nand_195_out, A_7, A_7);
  nand nand_196 (nand_196_out, C_7, C_7);
  nand nand_197 (nand_197_out, nand_161_out, nand_162_out);
  nand nand_198 (nand_198_out, B_3, nand_163_out);
  nand nand_199 (nand_199_out, A_3, C_3);
  nand nand_200 (nand_200_out, nand_164_out, C_3);
  nand nand_201 (nand_201_out, A_3, A_3);
  nand nand_202 (c_11, B_3, nand_165_out);
  nand nand_203 (nand_203_out, nand_166_out, nand_167_out);
  nand nand_204 (nand_204_out, B_3, nand_168_out);
  nand nand_205 (nand_205_out, A_3, nand_169_out, C_3);
  nand nand_206 (nand_206_out, nand_170_out, C_3);
  nand nand_207 (nand_207_out, B_3, nand_171_out);
  nand nand_208 (nand_208_out, nand_172_out, nand_173_out);
  nand nand_209 (nand_209_out, nand_174_out, C_3);
  nand nand_210 (nand_210_out, nand_175_out, nand_176_out);
  nand nand_211 (nand_211_out, nand_177_out, C_3);
  nand nand_212 (nand_212_out, A_3, B_3, nand_178_out);
  nand nand_213 (nand_213_out, nand_179_out, nand_180_out);
  nand nand_214 (nand_214_out, B_7, nand_181_out);
  nand nand_215 (nand_215_out, A_7, C_7);
  nand nand_216 (nand_216_out, nand_182_out, C_7);
  nand nand_217 (nand_217_out, A_7, A_7);
  nand nand_218 (c_15, B_7, nand_183_out);
  nand nand_219 (nand_219_out, nand_184_out, nand_185_out);
  nand nand_220 (nand_220_out, B_7, nand_186_out);
  nand nand_221 (nand_221_out, A_7, nand_187_out, C_7);
  nand nand_222 (nand_222_out, nand_188_out, C_7);
  nand nand_223 (nand_223_out, B_7, nand_189_out);
  nand nand_224 (nand_224_out, nand_190_out, nand_191_out);
  nand nand_225 (nand_225_out, nand_192_out, C_7);
  nand nand_226 (nand_226_out, nand_193_out, nand_194_out);
  nand nand_227 (nand_227_out, nand_195_out, C_7);
  nand nand_228 (nand_228_out, A_7, B_7, nand_196_out);
  nand nand_229 (a_11, nand_197_out, nand_198_out, nand_199_out);
  nand nand_230 (b_11, nand_200_out, nand_201_out);
  nand nand_231 (d_3, nand_203_out, nand_204_out, nand_205_out);
  nand nand_232 (e_3, nand_206_out, nand_207_out);
  nand nand_233 (f_3, nand_208_out, nand_209_out);
  nand nand_234 (g_3, nand_210_out, nand_211_out, nand_212_out);
  nand nand_235 (a_15, nand_213_out, nand_214_out, nand_215_out);
  nand nand_236 (b_15, nand_216_out, nand_217_out);
  nand nand_237 (d_7, nand_219_out, nand_220_out, nand_221_out);
  nand nand_238 (e_7, nand_222_out, nand_223_out);
  nand nand_239 (f_7, nand_224_out, nand_225_out);
  nand nand_240 (g_7, nand_226_out, nand_227_out, nand_228_out);
  _7_Segment_Display u_7_segment_display_5 (
    .g(g_3), .f(f_3), .a(a_11), .b(b_11), .e(e_3), .d(d_3), .c(c_11));  // open: dp
  _7_Segment_Display u_7_segment_display_6 (
    .g(g_7), .f(f_7), .a(a_15), .b(b_15), .e(e_7), .d(d_7), .c(c_15));  // open: dp
  nand nand_241 (nand_241_out, A_4, A_4);
  nand nand_242 (nand_242_out, B_4, B_4);
  nand nand_243 (nand_243_out, C_4, C_4);
  nand nand_244 (nand_244_out, B_4, B_4);
  nand nand_245 (nand_245_out, A_4, C_4);
  nand nand_246 (nand_246_out, A_4, A_4);
  nand nand_247 (nand_247_out, C_4, C_4);
  nand nand_248 (nand_248_out, C_4, C_4);
  nand nand_249 (nand_249_out, B_4, B_4);
  nand nand_250 (nand_250_out, B_4, B_4);
  nand nand_251 (nand_251_out, C_4, C_4);
  nand nand_252 (nand_252_out, A_4, A_4);
  nand nand_253 (nand_253_out, C_4, C_4);
  nand nand_254 (nand_254_out, B_4, B_4);
  nand nand_255 (nand_255_out, A_4, A_4);
  nand nand_256 (nand_256_out, B_4, B_4);
  nand nand_257 (nand_257_out, A_4, A_4);
  nand nand_258 (nand_258_out, C_4, C_4);
  nand nand_259 (nand_259_out, A_8, A_8);
  nand nand_260 (nand_260_out, B_8, B_8);
  nand nand_261 (nand_261_out, C_8, C_8);
  nand nand_262 (nand_262_out, B_8, B_8);
  nand nand_263 (nand_263_out, A_8, C_8);
  nand nand_264 (nand_264_out, A_8, A_8);
  nand nand_265 (nand_265_out, C_8, C_8);
  nand nand_266 (nand_266_out, C_8, C_8);
  nand nand_267 (nand_267_out, B_8, B_8);
  nand nand_268 (nand_268_out, B_8, B_8);
  nand nand_269 (nand_269_out, C_8, C_8);
  nand nand_270 (nand_270_out, A_8, A_8);
  nand nand_271 (nand_271_out, C_8, C_8);
  nand nand_272 (nand_272_out, B_8, B_8);
  nand nand_273 (nand_273_out, A_8, A_8);
  nand nand_274 (nand_274_out, B_8, B_8);
  nand nand_275 (nand_275_out, A_8, A_8);
  nand nand_276 (nand_276_out, C_8, C_8);
  nand nand_277 (nand_277_out, nand_241_out, nand_242_out);
  nand nand_278 (nand_278_out, B_4, nand_243_out);
  nand nand_279 (nand_279_out, A_4, C_4);
  nand nand_280 (nand_280_out, nand_244_out, C_4);
  nand nand_281 (nand_281_out, A_4, A_4);
  nand nand_282 (c_12, B_4, nand_245_out);
  nand nand_283 (nand_283_out, nand_246_out, nand_247_out);
  nand nand_284 (nand_284_out, B_4, nand_248_out);
  nand nand_285 (nand_285_out, A_4, nand_249_out, C_4);
  nand nand_286 (nand_286_out, nand_250_out, C_4);
  nand nand_287 (nand_287_out, B_4, nand_251_out);
  nand nand_288 (nand_288_out, nand_252_out, nand_253_out);
  nand nand_289 (nand_289_out, nand_254_out, C_4);
  nand nand_290 (nand_290_out, nand_255_out, nand_256_out);
  nand nand_291 (nand_291_out, nand_257_out, C_4);
  nand nand_292 (nand_292_out, A_4, B_4, nand_258_out);
  nand nand_293 (nand_293_out, nand_259_out, nand_260_out);
  nand nand_294 (nand_294_out, B_8, nand_261_out);
  nand nand_295 (nand_295_out, A_8, C_8);
  nand nand_296 (nand_296_out, nand_262_out, C_8);
  nand nand_297 (nand_297_out, A_8, A_8);
  nand nand_298 (c_16, B_8, nand_263_out);
  nand nand_299 (nand_299_out, nand_264_out, nand_265_out);
  nand nand_300 (nand_300_out, B_8, nand_266_out);
  nand nand_301 (nand_301_out, A_8, nand_267_out, C_8);
  nand nand_302 (nand_302_out, nand_268_out, C_8);
  nand nand_303 (nand_303_out, B_8, nand_269_out);
  nand nand_304 (nand_304_out, nand_270_out, nand_271_out);
  nand nand_305 (nand_305_out, nand_272_out, C_8);
  nand nand_306 (nand_306_out, nand_273_out, nand_274_out);
  nand nand_307 (nand_307_out, nand_275_out, C_8);
  nand nand_308 (nand_308_out, A_8, B_8, nand_276_out);
  nand nand_309 (a_12, nand_277_out, nand_278_out, nand_279_out);
  nand nand_310 (b_12, nand_280_out, nand_281_out);
  nand nand_311 (d_4, nand_283_out, nand_284_out, nand_285_out);
  nand nand_312 (e_4, nand_286_out, nand_287_out);
  nand nand_313 (f_4, nand_288_out, nand_289_out);
  nand nand_314 (g_4, nand_290_out, nand_291_out, nand_292_out);
  nand nand_315 (a_16, nand_293_out, nand_294_out, nand_295_out);
  nand nand_316 (b_16, nand_296_out, nand_297_out);
  nand nand_317 (d_8, nand_299_out, nand_300_out, nand_301_out);
  nand nand_318 (e_8, nand_302_out, nand_303_out);
  nand nand_319 (f_8, nand_304_out, nand_305_out);
  nand nand_320 (g_8, nand_306_out, nand_307_out, nand_308_out);
  _7_Segment_Display u_7_segment_display_7 (
    .g(g_4), .f(f_4), .a(a_12), .b(b_12), .e(e_4), .d(d_4), .c(c_12));  // open: dp
  _7_Segment_Display u_7_segment_display_8 (
    .g(g_8), .f(f_8), .a(a_16), .b(b_16), .e(e_8), .d(d_8), .c(c_16));  // open: dp

  // Notes on the sheet:
  //   Group 3
endmodule

module Sequential_2 (
  input  HIGH,
  output a,
  output b,
  output c,
  output d,
  output e,
  output f,
  output g
);

  wire and_1_out, and_2_out, and_3_out, and_4_out, and_5_out, and_6_out, and_7_out, and_8_out, and_9_out,
       and_10_out, and_11_out, and_12_out, and_13_out, and_14_out, and_15_out, CLOCK_out, JK0_q, JK1_q,
       JK2_q, not_1_out, not_2_out, not_3_out, not_4_out, not_5_out, not_6_out, not_7_out, not_8_out,
       not_9_out, not_10_out, not_11_out, not_12_out, not_13_out, not_14_out, not_15_out, not_16_out,
       not_17_out, not_18_out, Q1_Q0_out;

  Clock CLOCK (.out(CLOCK_out));
  J_K_Flip_Flop JK0 (.J(HIGH), .clk(CLOCK_out), .K(HIGH), .Q(JK0_q));  // open: Qn, preset, en, reset
  and Q1_Q0 (Q1_Q0_out, JK0_q, JK1_q);
  J_K_Flip_Flop JK1 (.J(JK0_q), .clk(CLOCK_out), .K(JK0_q), .Q(JK1_q));  // open: Qn, preset, en, reset
  J_K_Flip_Flop JK2 (.J(Q1_Q0_out), .clk(CLOCK_out), .K(Q1_Q0_out), .Q(JK2_q));  // open: Qn, preset, en, reset
  not not_1 (not_1_out, JK2_q);
  not not_2 (not_2_out, JK1_q);
  not not_3 (not_3_out, JK0_q);
  not not_4 (not_4_out, JK1_q);
  not not_5 (not_5_out, JK1_q);
  and and_1 (and_1_out, JK2_q, JK0_q);
  not not_6 (not_6_out, JK2_q);
  not not_7 (not_7_out, JK0_q);
  not not_8 (not_8_out, JK0_q);
  not not_9 (not_9_out, JK1_q);
  not not_10 (not_10_out, JK1_q);
  not not_11 (not_11_out, JK0_q);
  not not_12 (not_12_out, JK2_q);
  not not_13 (not_13_out, JK0_q);
  not not_14 (not_14_out, JK1_q);
  not not_15 (not_15_out, JK2_q);
  not not_16 (not_16_out, JK1_q);
  not not_17 (not_17_out, JK2_q);
  not not_18 (not_18_out, JK0_q);
  and and_2 (and_2_out, not_1_out, not_2_out);
  and and_3 (and_3_out, JK1_q, not_3_out);
  and and_4 (and_4_out, JK2_q, JK0_q);
  and and_5 (and_5_out, not_4_out, JK0_q);
  or or_1 (c, not_5_out, and_1_out);
  and and_6 (and_6_out, not_6_out, not_7_out);
  and and_7 (and_7_out, JK1_q, not_8_out);
  and and_8 (and_8_out, JK2_q, not_9_out, JK0_q);
  and and_9 (and_9_out, not_10_out, JK0_q);
  and and_10 (and_10_out, JK1_q, not_11_out);
  and and_11 (and_11_out, not_12_out, not_13_out);
  and and_12 (and_12_out, not_14_out, JK0_q);
  and and_13 (and_13_out, not_15_out, not_16_out);
  and and_14 (and_14_out, not_17_out, JK0_q);
  and and_15 (and_15_out, JK2_q, JK1_q, not_18_out);
  or or_2 (a, and_2_out, and_3_out, and_4_out);
  or or_3 (b, and_5_out, JK2_q);
  or or_4 (d, and_6_out, and_7_out, and_8_out);
  or or_5 (e, and_9_out, and_10_out);
  or or_6 (f, and_11_out, and_12_out);
  or or_7 (g, and_13_out, and_14_out, and_15_out);
  _7_Segment_Display u_7_segment_display_1 (.g(g), .f(f), .a(a), .b(b), .e(e), .d(d), .c(c));  // open: dp

  // Notes on the sheet:
  //   Group 3
  //   Md Ulfat Tahsin_1913057642
  //   Zannatul Ferdous Ananna_1921177042
  //   Tarikul Islam Saykat_1921832042
  //   Mariam Binte Bashir_2021874642
  //   A
  //   B
  //   C
endmodule

module Nor_Gates (
  input  A,
  input  A_2,
  input  A_3,
  input  A_4,
  input  B,
  input  A_5,
  input  B_2,
  input  B_3,
  input  A_6,
  input  A_7,
  input  a_8,
  input  C,
  input  B_4,
  input  C_2,
  input  C_3,
  input  B_5,
  input  B_6,
  input  B_7,
  input  B_8,
  input  C_4,
  input  C_5,
  input  C_6,
  input  C_7,
  input  C_8,
  output a_9,
  output a_10,
  output a_11,
  output a_12,
  output a_13,
  output a_14,
  output a_15,
  output a_16,
  output b_9,
  output b_10,
  output b_11,
  output b_12,
  output b_13,
  output b_14,
  output b_15,
  output b_16,
  output c_9,
  output c_10,
  output c_11,
  output c_12,
  output c_13,
  output c_14,
  output c_15,
  output c_16,
  output d,
  output d_2,
  output d_3,
  output d_4,
  output d_5,
  output d_6,
  output d_7,
  output d_8,
  output e,
  output e_2,
  output e_3,
  output e_4,
  output e_5,
  output e_6,
  output e_7,
  output e_8,
  output f,
  output f_2,
  output f_3,
  output f_4,
  output f_5,
  output f_6,
  output f_7,
  output f_8,
  output out_73,
  output out_74,
  output out_75,
  output out_76,
  output out_77,
  output out_78,
  output out_79,
  output out_80
);

  wire nor_1_out, nor_2_out, nor_3_out, nor_4_out, nor_5_out, nor_6_out, nor_7_out, nor_8_out, nor_9_out,
       nor_10_out, nor_11_out, nor_12_out, nor_13_out, nor_14_out, nor_15_out, nor_16_out, nor_17_out,
       nor_25_out, nor_26_out, nor_27_out, nor_28_out, nor_29_out, nor_30_out, nor_31_out, nor_32_out,
       nor_33_out, nor_34_out, nor_35_out, nor_36_out, nor_37_out, nor_38_out, nor_39_out, nor_40_out,
       nor_41_out, nor_49_out, nor_50_out, nor_51_out, nor_52_out, nor_53_out, nor_54_out, nor_55_out,
       nor_56_out, nor_57_out, nor_58_out, nor_59_out, nor_60_out, nor_61_out, nor_62_out, nor_63_out,
       nor_64_out, nor_65_out, nor_73_out, nor_74_out, nor_75_out, nor_76_out, nor_77_out, nor_78_out,
       nor_79_out, nor_80_out, nor_81_out, nor_82_out, nor_83_out, nor_84_out, nor_85_out, nor_86_out,
       nor_87_out, nor_88_out, nor_89_out, nor_97_out, nor_98_out, nor_99_out, nor_100_out, nor_101_out,
       nor_102_out, nor_103_out, nor_104_out, nor_105_out, nor_106_out, nor_107_out, nor_108_out,
       nor_109_out, nor_110_out, nor_111_out, nor_112_out, nor_113_out, nor_121_out, nor_122_out,
       nor_123_out, nor_124_out, nor_125_out, nor_126_out, nor_127_out, nor_128_out, nor_129_out,
       nor_130_out, nor_131_out, nor_132_out, nor_133_out, nor_134_out, nor_135_out, nor_136_out,
       nor_137_out, nor_145_out, nor_146_out, nor_147_out, nor_148_out, nor_149_out, nor_150_out,
       nor_151_out, nor_152_out, nor_153_out, nor_154_out, nor_155_out, nor_156_out, nor_157_out,
       nor_158_out, nor_159_out, nor_160_out, nor_161_out, nor_169_out, nor_170_out, nor_171_out,
       nor_172_out, nor_173_out, nor_174_out, nor_175_out, nor_176_out, nor_177_out, nor_178_out,
       nor_179_out, nor_180_out, nor_181_out, nor_182_out, nor_183_out, nor_184_out, nor_185_out, not_1_out,
       not_2_out, not_3_out, not_4_out, not_5_out, not_6_out, not_7_out, not_8_out, not_9_out, not_10_out,
       not_11_out, not_12_out, not_13_out, not_14_out, not_15_out, not_16_out, not_17_out, not_18_out,
       not_19_out, not_20_out, not_21_out, not_22_out, not_23_out, not_24_out, not_25_out, not_26_out,
       not_27_out, not_28_out, not_29_out, not_30_out, not_31_out, not_32_out, not_33_out, not_34_out,
       not_35_out, not_36_out, not_37_out, not_38_out, not_39_out, not_40_out, not_41_out, not_42_out,
       not_43_out, not_44_out, not_45_out, not_46_out, not_47_out, not_48_out, not_49_out, not_50_out,
       not_51_out, not_52_out, not_53_out, not_54_out, not_55_out, not_56_out, not_57_out, not_58_out,
       not_59_out, not_60_out, not_61_out, not_62_out, not_63_out, not_64_out, not_65_out, not_66_out,
       not_67_out, not_68_out, not_69_out, not_70_out, not_71_out, not_72_out, not_73_out, not_74_out,
       not_75_out, not_76_out, not_77_out, not_78_out, not_79_out, not_80_out, not_81_out, not_82_out,
       not_83_out, not_84_out, not_85_out, not_86_out, not_87_out, not_88_out, not_89_out, not_90_out,
       not_91_out, not_92_out, not_93_out, not_94_out, not_95_out, not_96_out, not_97_out, not_98_out,
       not_99_out, not_100_out, not_101_out, not_102_out, not_103_out, not_104_out, not_105_out, not_106_out,
       not_107_out, not_108_out, not_109_out, not_110_out, not_111_out, not_112_out, not_113_out,
       not_114_out, not_115_out, not_116_out, not_117_out, not_118_out, not_119_out, not_120_out,
       not_121_out, not_122_out, not_123_out, not_124_out, not_125_out, not_126_out, not_127_out,
       not_128_out, not_129_out, not_130_out, not_131_out, not_132_out, not_133_out, not_134_out,
       not_135_out, not_136_out, not_137_out, not_138_out, not_139_out, not_140_out, not_141_out,
       not_142_out, not_143_out, not_144_out, not_145_out, not_146_out, not_147_out, not_148_out,
       not_149_out, not_150_out, not_151_out, not_152_out, not_153_out, not_154_out, not_155_out,
       not_156_out, not_157_out, not_158_out, not_159_out, not_160_out, not_161_out, not_162_out,
       not_163_out, not_164_out, not_165_out, not_166_out, not_167_out, not_168_out;

  not not_1 (not_1_out, B);
  not not_2 (not_2_out, C);
  not not_3 (not_3_out, B);
  not not_4 (not_4_out, B);
  not not_5 (not_5_out, B);
  not not_6 (not_6_out, C);
  not not_7 (not_7_out, B);
  not not_8 (not_8_out, C);
  not not_9 (not_9_out, A);
  not not_10 (not_10_out, B);
  not not_11 (not_11_out, C);
  not not_12 (not_12_out, B);
  not not_13 (not_13_out, C);
  not not_14 (not_14_out, A);
  not not_15 (not_15_out, A);
  not not_16 (not_16_out, B);
  not not_17 (not_17_out, B);
  not not_18 (not_18_out, A);
  not not_19 (not_19_out, C);
  not not_20 (not_20_out, A);
  nor nor_1 (nor_1_out, A, not_1_out, not_2_out);
  not not_21 (not_21_out, A);
  nor nor_2 (nor_2_out, not_21_out, B, C);
  nor nor_3 (nor_3_out, A, C);
  nor nor_4 (nor_4_out, A, not_3_out);
  nor nor_5 (nor_5_out, A, not_4_out);
  nor nor_6 (nor_6_out, not_5_out, C);
  nor nor_7 (nor_7_out, A, not_6_out);
  nor nor_8 (nor_8_out, not_7_out, not_8_out);
  nor nor_9 (nor_9_out, not_9_out, B, C);
  nor nor_10 (nor_10_out, B, C);
  nor nor_11 (nor_11_out, not_10_out, not_11_out);
  nor nor_12 (nor_12_out, not_12_out, not_13_out);
  nor nor_13 (nor_13_out, not_14_out, C);
  nor nor_14 (nor_14_out, not_15_out, not_16_out);
  nor nor_15 (nor_15_out, A, not_17_out, C);
  nor nor_16 (nor_16_out, not_18_out, not_19_out);
  nor nor_17 (nor_17_out, not_20_out, B);
  nor nor_18 (a_9, nor_1_out, nor_2_out);
  nor nor_19 (b_9, nor_3_out, nor_4_out);
  nor nor_20 (c_9, nor_5_out, nor_6_out);
  nor nor_21 (d, nor_7_out, nor_8_out, nor_9_out);
  nor nor_22 (e, nor_10_out, nor_11_out);
  nor nor_23 (f, nor_12_out, nor_13_out, nor_14_out);
  nor nor_24 (out_73, nor_15_out, nor_16_out, nor_17_out);
  _7_Segment_Display u_7_segment_display_1 (.g(out_73), .f(f), .a(a_9), .b(b_9), .e(e), .d(d), .c(c_9));  // open: dp
  not not_22 (not_22_out, B_2);
  not not_23 (not_23_out, C_2);
  not not_24 (not_24_out, B_2);
  not not_25 (not_25_out, B_2);
  not not_26 (not_26_out, B_2);
  not not_27 (not_27_out, B_2);
  not not_28 (not_28_out, C_2);
  not not_29 (not_29_out, A_2);
  not not_30 (not_30_out, B_2);
  not not_31 (not_31_out, C_2);
  not not_32 (not_32_out, B_2);
  not not_33 (not_33_out, C_2);
  not not_34 (not_34_out, A_2);
  not not_35 (not_35_out, A_2);
  not not_36 (not_36_out, B_2);
  not not_37 (not_37_out, B_2);
  not not_38 (not_38_out, A_2);
  not not_39 (not_39_out, C_2);
  not not_40 (not_40_out, A_2);
  nor nor_25 (nor_25_out, A_2, not_22_out, not_23_out);
  not not_41 (not_41_out, A_2);
  not not_42 (not_42_out, C_2);
  nor nor_26 (nor_26_out, not_41_out, B_2, C_2);
  nor nor_27 (nor_27_out, A_2, C_2);
  nor nor_28 (nor_28_out, A_2, not_24_out);
  nor nor_29 (nor_29_out, A_2, not_25_out);
  nor nor_30 (nor_30_out, not_26_out, C_2);
  nor nor_31 (nor_31_out, A_2, not_42_out);
  nor nor_32 (nor_32_out, not_27_out, not_28_out);
  nor nor_33 (nor_33_out, not_29_out, B_2, C_2);
  nor nor_34 (nor_34_out, B_2, C_2);
  nor nor_35 (nor_35_out, not_30_out, not_31_out);
  nor nor_36 (nor_36_out, not_32_out, not_33_out);
  nor nor_37 (nor_37_out, not_34_out, C_2);
  nor nor_38 (nor_38_out, not_35_out, not_36_out);
  nor nor_39 (nor_39_out, A_2, not_37_out, C_2);
  nor nor_40 (nor_40_out, not_38_out, not_39_out);
  nor nor_41 (nor_41_out, not_40_out, B_2);
  nor nor_42 (a_10, nor_25_out, nor_26_out);
  nor nor_43 (b_10, nor_27_out, nor_28_out);
  nor nor_44 (c_10, nor_29_out, nor_30_out);
  nor nor_45 (d_2, nor_31_out, nor_32_out, nor_33_out);
  nor nor_46 (e_2, nor_34_out, nor_35_out);
  nor nor_47 (f_2, nor_36_out, nor_37_out, nor_38_out);
  nor nor_48 (out_74, nor_39_out, nor_40_out, nor_41_out);
  _7_Segment_Display u_7_segment_display_2 (
    .g(out_74), .f(f_2), .a(a_10), .b(b_10), .e(e_2), .d(d_2), .c(c_10));  // open: dp
  not not_43 (not_43_out, B_3);
  not not_44 (not_44_out, C_3);
  not not_45 (not_45_out, B_3);
  not not_46 (not_46_out, B_3);
  not not_47 (not_47_out, B_3);
  not not_48 (not_48_out, C_3);
  not not_49 (not_49_out, B_3);
  not not_50 (not_50_out, C_3);
  not not_51 (not_51_out, A_3);
  not not_52 (not_52_out, B_3);
  not not_53 (not_53_out, C_3);
  not not_54 (not_54_out, B_3);
  not not_55 (not_55_out, C_3);
  not not_56 (not_56_out, A_3);
  not not_57 (not_57_out, A_3);
  not not_58 (not_58_out, B_3);
  not not_59 (not_59_out, B_3);
  not not_60 (not_60_out, A_3);
  not not_61 (not_61_out, C_3);
  not not_62 (not_62_out, A_3);
  nor nor_49 (nor_49_out, A_3, not_43_out, not_44_out);
  not not_63 (not_63_out, A_3);
  nor nor_50 (nor_50_out, not_63_out, B_3, C_3);
  nor nor_51 (nor_51_out, A_3, C_3);
  nor nor_52 (nor_52_out, A_3, not_45_out);
  nor nor_53 (nor_53_out, A_3, not_46_out);
  nor nor_54 (nor_54_out, not_47_out, C_3);
  nor nor_55 (nor_55_out, A_3, not_48_out);
  nor nor_56 (nor_56_out, not_49_out, not_50_out);
  nor nor_57 (nor_57_out, not_51_out, B_3, C_3);
  nor nor_58 (nor_58_out, B_3, C_3);
  nor nor_59 (nor_59_out, not_52_out, not_53_out);
  nor nor_60 (nor_60_out, not_54_out, not_55_out);
  nor nor_61 (nor_61_out, not_56_out, C_3);
  nor nor_62 (nor_62_out, not_57_out, not_58_out);
  nor nor_63 (nor_63_out, A_3, not_59_out, C_3);
  nor nor_64 (nor_64_out, not_60_out, not_61_out);
  nor nor_65 (nor_65_out, not_62_out, B_3);
  nor nor_66 (a_11, nor_49_out, nor_50_out);
  nor nor_67 (b_11, nor_51_out, nor_52_out);
  nor nor_68 (c_11, nor_53_out, nor_54_out);
  nor nor_69 (d_3, nor_55_out, nor_56_out, nor_57_out);
  nor nor_70 (e_3, nor_58_out, nor_59_out);
  nor nor_71 (f_3, nor_60_out, nor_61_out, nor_62_out);
  nor nor_72 (out_75, nor_63_out, nor_64_out, nor_65_out);
  _7_Segment_Display u_7_segment_display_3 (
    .g(out_75), .f(f_3), .a(a_11), .b(b_11), .e(e_3), .d(d_3), .c(c_11));  // open: dp
  not not_64 (not_64_out, B_4);
  not not_65 (not_65_out, C_4);
  not not_66 (not_66_out, B_4);
  not not_67 (not_67_out, C_4);
  not not_68 (not_68_out, A_4);
  nor nor_73 (nor_73_out, A_4, not_64_out, not_65_out);
  not not_69 (not_69_out, A_4);
  not not_70 (not_70_out, B_4);
  not not_71 (not_71_out, B_4);
  not not_72 (not_72_out, B_4);
  not not_73 (not_73_out, C_4);
  not not_74 (not_74_out, B_4);
  not not_75 (not_75_out, C_4);
  not not_76 (not_76_out, B_4);
  not not_77 (not_77_out, C_4);
  not not_78 (not_78_out, A_4);
  not not_79 (not_79_out, A_4);
  not not_80 (not_80_out, B_4);
  not not_81 (not_81_out, B_4);
  not not_82 (not_82_out, A_4);
  not not_83 (not_83_out, C_4);
  not not_84 (not_84_out, A_4);
  nor nor_74 (nor_74_out, not_69_out, B_4, C_4);
  nor nor_75 (nor_75_out, A_4, C_4);
  nor nor_76 (nor_76_out, A_4, not_70_out);
  nor nor_77 (nor_77_out, A_4, not_71_out);
  nor nor_78 (nor_78_out, not_72_out, C_4);
  nor nor_79 (nor_79_out, A_4, not_73_out);
  nor nor_80 (nor_80_out, not_66_out, not_67_out);
  nor nor_81 (nor_81_out, not_68_out, B_4, C_4);
  nor nor_82 (nor_82_out, B_4, C_4);
  nor nor_83 (nor_83_out, not_74_out, not_75_out);
  nor nor_84 (nor_84_out, not_76_out, not_77_out);
  nor nor_85 (nor_85_out, not_78_out, C_4);
  nor nor_86 (nor_86_out, not_79_out, not_80_out);
  nor nor_87 (nor_87_out, A_4, not_81_out, C_4);
  nor nor_88 (nor_88_out, not_82_out, not_83_out);
  nor nor_89 (nor_89_out, not_84_out, B_4);
  nor nor_90 (a_12, nor_73_out, nor_74_out);
  nor nor_91 (b_12, nor_75_out, nor_76_out);
  nor nor_92 (c_12, nor_77_out, nor_78_out);
  nor nor_93 (d_4, nor_79_out, nor_80_out, nor_81_out);
  nor nor_94 (e_4, nor_82_out, nor_83_out);
  nor nor_95 (f_4, nor_84_out, nor_85_out, nor_86_out);
  nor nor_96 (out_76, nor_87_out, nor_88_out, nor_89_out);
  _7_Segment_Display u_7_segment_display_4 (
    .g(out_76), .f(f_4), .a(a_12), .b(b_12), .e(e_4), .d(d_4), .c(c_12));  // open: dp
  not not_85 (not_85_out, B_8);
  not not_86 (not_86_out, C_8);
  not not_87 (not_87_out, B_8);
  not not_88 (not_88_out, B_8);
  not not_89 (not_89_out, B_8);
  not not_90 (not_90_out, B_8);
  not not_91 (not_91_out, C_8);
  not not_92 (not_92_out, a_8);
  not not_93 (not_93_out, B_8);
  not not_94 (not_94_out, C_8);
  not not_95 (not_95_out, B_8);
  not not_96 (not_96_out, C_8);
  not not_97 (not_97_out, a_8);
  not not_98 (not_98_out, a_8);
  not not_99 (not_99_out, B_8);
  not not_100 (not_100_out, B_8);
  not not_101 (not_101_out, a_8);
  not not_102 (not_102_out, C_8);
  not not_103 (not_103_out, a_8);
  nor nor_97 (nor_97_out, a_8, not_85_out, not_86_out);
  not not_104 (not_104_out, a_8);
  not not_105 (not_105_out, C_8);
  nor nor_98 (nor_98_out, not_104_out, B_8, C_8);
  nor nor_99 (nor_99_out, a_8, C_8);
  nor nor_100 (nor_100_out, a_8, not_87_out);
  nor nor_101 (nor_101_out, a_8, not_88_out);
  nor nor_102 (nor_102_out, not_89_out, C_8);
  nor nor_103 (nor_103_out, a_8, not_105_out);
  nor nor_104 (nor_104_out, not_90_out, not_91_out);
  nor nor_105 (nor_105_out, not_92_out, B_8, C_8);
  nor nor_106 (nor_106_out, B_8, C_8);
  nor nor_107 (nor_107_out, not_93_out, not_94_out);
  nor nor_108 (nor_108_out, not_95_out, not_96_out);
  nor nor_109 (nor_109_out, not_97_out, C_8);
  nor nor_110 (nor_110_out, not_98_out, not_99_out);
  nor nor_111 (nor_111_out, a_8, not_100_out, C_8);
  nor nor_112 (nor_112_out, not_101_out, not_102_out);
  nor nor_113 (nor_113_out, not_103_out, B_8);
  nor nor_114 (a_16, nor_97_out, nor_98_out);
  nor nor_115 (b_16, nor_99_out, nor_100_out);
  nor nor_116 (c_16, nor_101_out, nor_102_out);
  nor nor_117 (d_8, nor_103_out, nor_104_out, nor_105_out);
  nor nor_118 (e_8, nor_106_out, nor_107_out);
  nor nor_119 (f_8, nor_108_out, nor_109_out, nor_110_out);
  nor nor_120 (out_80, nor_111_out, nor_112_out, nor_113_out);
  _7_Segment_Display u_7_segment_display_5 (
    .g(out_80), .f(f_8), .a(a_16), .b(b_16), .e(e_8), .d(d_8), .c(c_16));  // open: dp
  not not_106 (not_106_out, B_5);
  not not_107 (not_107_out, C_5);
  not not_108 (not_108_out, B_5);
  not not_109 (not_109_out, C_5);
  not not_110 (not_110_out, A_5);
  nor nor_121 (nor_121_out, A_5, not_106_out, not_107_out);
  not not_111 (not_111_out, A_5);
  not not_112 (not_112_out, B_5);
  not not_113 (not_113_out, B_5);
  not not_114 (not_114_out, B_5);
  not not_115 (not_115_out, C_5);
  not not_116 (not_116_out, B_5);
  not not_117 (not_117_out, C_5);
  not not_118 (not_118_out, B_5);
  not not_119 (not_119_out, C_5);
  not not_120 (not_120_out, A_5);
  not not_121 (not_121_out, A_5);
  not not_122 (not_122_out, B_5);
  not not_123 (not_123_out, B_5);
  not not_124 (not_124_out, A_5);
  not not_125 (not_125_out, C_5);
  not not_126 (not_126_out, A_5);
  nor nor_122 (nor_122_out, not_111_out, B_5, C_5);
  nor nor_123 (nor_123_out, A_5, C_5);
  nor nor_124 (nor_124_out, A_5, not_112_out);
  nor nor_125 (nor_125_out, A_5, not_113_out);
  nor nor_126 (nor_126_out, not_114_out, C_5);
  nor nor_127 (nor_127_out, A_5, not_115_out);
  nor nor_128 (nor_128_out, not_108_out, not_109_out);
  nor nor_129 (nor_129_out, not_110_out, B_5, C_5);
  nor nor_130 (nor_130_out, B_5, C_5);
  nor nor_131 (nor_131_out, not_116_out, not_117_out);
  nor nor_132 (nor_132_out, not_118_out, not_119_out);
  nor nor_133 (nor_133_out, not_120_out, C_5);
  nor nor_134 (nor_134_out, not_121_out, not_122_out);
  nor nor_135 (nor_135_out, A_5, not_123_out, C_5);
  nor nor_136 (nor_136_out, not_124_out, not_125_out);
  nor nor_137 (nor_137_out, not_126_out, B_5);
  nor nor_138 (a_13, nor_121_out, nor_122_out);
  nor nor_139 (b_13, nor_123_out, nor_124_out);
  nor nor_140 (c_13, nor_125_out, nor_126_out);
  nor nor_141 (d_5, nor_127_out, nor_128_out, nor_129_out);
  nor nor_142 (e_5, nor_130_out, nor_131_out);
  nor nor_143 (f_5, nor_132_out, nor_133_out, nor_134_out);
  nor nor_144 (out_77, nor_135_out, nor_136_out, nor_137_out);
  _7_Segment_Display u_7_segment_display_6 (
    .g(out_77), .f(f_5), .a(a_13), .b(b_13), .e(e_5), .d(d_5), .c(c_13));  // open: dp
  not not_127 (not_127_out, B_6);
  not not_128 (not_128_out, C_6);
  not not_129 (not_129_out, A_6);
  not not_130 (not_130_out, B_6);
  not not_131 (not_131_out, B_6);
  not not_132 (not_132_out, B_6);
  not not_133 (not_133_out, C_6);
  not not_134 (not_134_out, B_6);
  not not_135 (not_135_out, C_6);
  not not_136 (not_136_out, A_6);
  not not_137 (not_137_out, B_6);
  not not_138 (not_138_out, C_6);
  not not_139 (not_139_out, B_6);
  not not_140 (not_140_out, C_6);
  not not_141 (not_141_out, A_6);
  not not_142 (not_142_out, A_6);
  not not_143 (not_143_out, B_6);
  not not_144 (not_144_out, B_6);
  not not_145 (not_145_out, A_6);
  not not_146 (not_146_out, C_6);
  not not_147 (not_147_out, A_6);
  nor nor_145 (nor_145_out, A_6, not_127_out, not_128_out);
  nor nor_146 (nor_146_out, not_129_out, B_6, C_6);
  nor nor_147 (nor_147_out, A_6, C_6);
  nor nor_148 (nor_148_out, A_6, not_130_out);
  nor nor_149 (nor_149_out, A_6, not_131_out);
  nor nor_150 (nor_150_out, not_132_out, C_6);
  nor nor_151 (nor_151_out, A_6, not_133_out);
  nor nor_152 (nor_152_out, not_134_out, not_135_out);
  nor nor_153 (nor_153_out, not_136_out, B_6, C_6);
  nor nor_154 (nor_154_out, B_6, C_6);
  nor nor_155 (nor_155_out, not_137_out, not_138_out);
  nor nor_156 (nor_156_out, not_139_out, not_140_out);
  nor nor_157 (nor_157_out, not_141_out, C_6);
  nor nor_158 (nor_158_out, not_142_out, not_143_out);
  nor nor_159 (nor_159_out, A_6, not_144_out, C_6);
  nor nor_160 (nor_160_out, not_145_out, not_146_out);
  nor nor_161 (nor_161_out, not_147_out, B_6);
  nor nor_162 (a_14, nor_145_out, nor_146_out);
  nor nor_163 (b_14, nor_147_out, nor_148_out);
  nor nor_164 (c_14, nor_149_out, nor_150_out);
  nor nor_165 (d_6, nor_151_out, nor_152_out, nor_153_out);
  nor nor_166 (e_6, nor_154_out, nor_155_out);
  nor nor_167 (f_6, nor_156_out, nor_157_out, nor_158_out);
  nor nor_168 (out_78, nor_159_out, nor_160_out, nor_161_out);
  _7_Segment_Display u_7_segment_display_7 (
    .g(out_78), .f(f_6), .a(a_14), .b(b_14), .e(e_6), .d(d_6), .c(c_14));  // open: dp
  not not_148 (not_148_out, B_7);
  not not_149 (not_149_out, C_7);
  not not_150 (not_150_out, A_7);
  not not_151 (not_151_out, B_7);
  not not_152 (not_152_out, B_7);
  not not_153 (not_153_out, B_7);
  not not_154 (not_154_out, C_7);
  not not_155 (not_155_out, B_7);
  not not_156 (not_156_out, C_7);
  not not_157 (not_157_out, A_7);
  not not_158 (not_158_out, B_7);
  not not_159 (not_159_out, C_7);
  not not_160 (not_160_out, B_7);
  not not_161 (not_161_out, C_7);
  not not_162 (not_162_out, A_7);
  not not_163 (not_163_out, A_7);
  not not_164 (not_164_out, B_7);
  not not_165 (not_165_out, B_7);
  not not_166 (not_166_out, A_7);
  not not_167 (not_167_out, C_7);
  not not_168 (not_168_out, A_7);
  nor nor_169 (nor_169_out, A_7, not_148_out, not_149_out);
  nor nor_170 (nor_170_out, not_150_out, B_7, C_7);
  nor nor_171 (nor_171_out, A_7, C_7);
  nor nor_172 (nor_172_out, A_7, not_151_out);
  nor nor_173 (nor_173_out, A_7, not_152_out);
  nor nor_174 (nor_174_out, not_153_out, C_7);
  nor nor_175 (nor_175_out, A_7, not_154_out);
  nor nor_176 (nor_176_out, not_155_out, not_156_out);
  nor nor_177 (nor_177_out, not_157_out, B_7, C_7);
  nor nor_178 (nor_178_out, B_7, C_7);
  nor nor_179 (nor_179_out, not_158_out, not_159_out);
  nor nor_180 (nor_180_out, not_160_out, not_161_out);
  nor nor_181 (nor_181_out, not_162_out, C_7);
  nor nor_182 (nor_182_out, not_163_out, not_164_out);
  nor nor_183 (nor_183_out, A_7, not_165_out, C_7);
  nor nor_184 (nor_184_out, not_166_out, not_167_out);
  nor nor_185 (nor_185_out, not_168_out, B_7);
  nor nor_186 (a_15, nor_169_out, nor_170_out);
  nor nor_187 (b_15, nor_171_out, nor_172_out);
  nor nor_188 (c_15, nor_173_out, nor_174_out);
  nor nor_189 (d_7, nor_175_out, nor_176_out, nor_177_out);
  nor nor_190 (e_7, nor_178_out, nor_179_out);
  nor nor_191 (f_7, nor_180_out, nor_181_out, nor_182_out);
  nor nor_192 (out_79, nor_183_out, nor_184_out, nor_185_out);
  _7_Segment_Display u_7_segment_display_8 (
    .g(out_79), .f(f_7), .a(a_15), .b(b_15), .e(e_7), .d(d_7), .c(c_15));  // open: dp

  // Notes on the sheet:
  //   a
  //   a
  //   g
  //   a
  //   a
  //   g
  //   Group 3
  //   a
  //   a
  //   a
  //   a
  //   a
  //   g
  //   Group 3
  //   a
  //   g
  //   A
  //   g
  //   g
  //   g
  //   g
endmodule
